// Logisim project Example2-13SimplifyingProductOfSums.circ as structural Verilog: 3 circuits, main circuit main
module main (
  input  A,
  input  B,
  input  C,
  input  D
);
endmodule

module Test (
  input  A,
  input  B,
  input  C,
  input  D,
  output F
);
endmodule

module _2_13 (
  input  A,
  input  B,
  input  C,
  input  D,
  output F
);

  wire not_1_out, not_2_out, not_3_out, not_4_out, not_5_out, or_1_out, or_2_out, or_3_out;

  not not_1 (not_1_out, A);
  or or_1 (or_1_out, not_1_out, not_2_out);
  not not_2 (not_2_out, B);
  not not_3 (not_3_out, C);
  or or_2 (or_2_out, not_3_out, not_4_out);
  not not_4 (not_4_out, D);
  not not_5 (not_5_out, B);
  or or_3 (or_3_out, not_5_out, D);
  and and_1 (F, or_1_out, or_2_out, or_3_out);
endmodule
