// Logisim project Example2-3Dual.circ as structural Verilog: 1 circuit, main circuit main
module main (
  input  x,
  input  y,
  input  z,
  output f
);

  wire not_1_out, not_2_out, not_3_out, not_4_out, or_1_out, or_2_out;

  not not_1 (not_1_out, x);
  not not_2 (not_2_out, z);
  not not_3 (not_3_out, x);
  not not_4 (not_4_out, y);
  or or_1 (or_1_out, not_1_out, y, not_2_out);
  or or_2 (or_2_out, not_3_out, not_4_out, z);
  and and_1 (f, or_1_out, or_2_out);
endmodule
