// Logisim project Example2-6OptimizationWithKarnough.circ as structural Verilog: 1 circuit, main circuit main
module main (
  input  a,
  input  b,
  input  c,
  output out_4
);

  wire and_1_out, not_1_out, not_2_out;

  not not_1 (not_1_out, b);
  and and_1 (and_1_out, a, not_1_out);
  not not_2 (not_2_out, c);
  or or_1 (out_4, and_1_out, not_2_out);
endmodule
