// Logisim project Figure23-AndOrInvert.circ as structural Verilog: 1 circuit, main circuit main
module main (
  input  W,
  input  X,
  input  Y,
  input  Z,
  output out_5
);

  wire and_1_out, and_2_out;

  and and_1 (and_1_out, W, X);
  and and_2 (and_2_out, Y, Z);
  nor nor_1 (out_5, and_1_out, and_2_out);
endmodule
