// Logisim project Figure23-OrAndInvert.circ as structural Verilog: 1 circuit, main circuit main
module main (
  input  W,
  input  X,
  input  Y,
  input  Z,
  output out_5
);

  wire or_1_out, or_2_out;

  or or_1 (or_1_out, W, X);
  or or_2 (or_2_out, Y, Z);
  nand nand_1 (out_5, or_1_out, or_2_out);
endmodule
