// Logisim project Figure24-And.circ as structural Verilog: 1 circuit, main circuit main
module main (
  input  X,
  input  Y,
  output out_3
);

  wire nand_1_out;

  nand nand_1 (nand_1_out, X, Y);
  not not_1 (out_3, nand_1_out);
endmodule
