// Logisim project Figure24-Or.circ as structural Verilog: 1 circuit, main circuit main
module main (
  input  X,
  input  Y,
  output out_3
);

  wire not_1_out, not_2_out;

  not not_1 (not_1_out, X);
  not not_2 (not_2_out, Y);
  nand nand_1 (out_3, not_1_out, not_2_out);
endmodule
