// Logisim project EXampe3-9CarElectricalControlUsingEnabling.circ as structural Verilog: 1 circuit, main circuit main
module main (
  input  IS,
  input  LS,
  input  RS,
  input  WS,
  output L,
  output R,
  output W
);

  and and_1 (L, LS, IS);
  and and_2 (R, RS, IS);
  and and_3 (W, WS, IS);
endmodule
