// Logisim project Example3-1BCDToExcess3CodeConverter.circ as structural Verilog: 1 circuit, main circuit main
module main (
  input  A,
  input  B,
  input  C,
  input  D,
  output out_5,
  output out_6,
  output out_7,
  output out_8
);

  wire and_1_out, and_2_out, and_3_out, and_4_out, not_1_out, not_3_out, or_1_out;

  not not_1 (not_1_out, B);
  or or_1 (or_1_out, C, D);
  not not_2 (out_8, D);
  not not_3 (not_3_out, or_1_out);
  and and_1 (and_1_out, C, D);
  and and_2 (and_2_out, B, or_1_out);
  and and_3 (and_3_out, not_1_out, or_1_out);
  and and_4 (and_4_out, B, not_3_out);
  or or_2 (out_5, A, and_2_out);
  or or_3 (out_6, and_3_out, and_4_out);
  or or_4 (out_7, and_4_out, and_1_out);
endmodule
