// Logisim project Example3-2BCDToSevenSegmentDecoder.circ as structural Verilog: 1 circuit, main circuit main
module main (
  input  A,
  input  B,
  input  C,
  input  D,
  output a_2,
  output b_2,
  output c_2,
  output d_2,
  output e,
  output f,
  output g
);

  wire nand_1_out, nand_2_out, nand_3_out, nand_4_out, nand_5_out, nand_6_out, nand_7_out, nand_8_out,
       nand_9_out, nand_10_out, nand_11_out, nand_12_out, nand_13_out, nand_14_out, nand_15_out, nand_16_out,
       nand_17_out, nand_18_out, nand_19_out, nand_20_out, nand_21_out, nand_22_out, nand_23_out,
       nand_24_out, nand_25_out, nand_26_out, nand_27_out, nand_28_out, nand_29_out, nand_30_out,
       nand_31_out, nand_32_out, nand_33_out, nand_34_out, nand_35_out, nand_36_out, nand_37_out,
       nand_38_out, nand_39_out, nand_40_out, nand_41_out, nand_42_out, nand_43_out, nand_44_out,
       nand_45_out, nand_46_out, nand_47_out, nand_48_out, nand_49_out, nand_50_out, nand_51_out,
       nand_52_out, nand_53_out, nand_54_out, nand_55_out, nand_56_out, nand_57_out, nand_58_out,
       nand_59_out, nand_60_out, nand_61_out, nand_62_out, nand_63_out, nand_64_out, nand_65_out,
       nand_66_out, nand_67_out, nand_68_out, nand_69_out, nand_70_out, nand_71_out, nand_72_out,
       nand_73_out, nand_74_out, nand_75_out, nand_76_out, nand_77_out, nand_78_out, nand_79_out,
       nand_80_out, nand_81_out, nand_82_out, nand_83_out, nand_84_out, nand_85_out, nand_86_out,
       nand_87_out, nand_88_out, nand_89_out, nand_90_out, nand_91_out, nand_92_out, nand_93_out,
       nand_94_out, nand_95_out, nand_96_out, nand_97_out, nand_98_out, nand_99_out, nand_100_out,
       nand_101_out, nand_102_out, nand_103_out, nand_104_out, nand_105_out, nand_106_out, nand_107_out,
       nand_108_out, nand_109_out, nand_110_out, nand_111_out, nand_112_out, nand_113_out, nand_114_out,
       nand_115_out, nand_116_out, nand_117_out, nand_118_out, nand_119_out, nand_120_out, nand_121_out,
       nand_122_out, nand_123_out, nand_124_out, nand_125_out, nand_126_out, nand_127_out, nand_128_out,
       nand_129_out, nand_130_out, nand_131_out, nand_132_out, nand_133_out, nand_134_out, nand_136_out,
       nand_137_out, nand_138_out, nand_139_out, nand_140_out, nand_141_out, nand_142_out, nand_143_out,
       nand_144_out, nand_145_out, nand_146_out, nand_147_out, nand_148_out, nand_149_out, nand_150_out,
       nand_151_out, nand_152_out, nand_153_out, nand_157_out, nand_158_out, nand_161_out, nand_162_out;

  nand nand_1 (nand_1_out, A, A);
  nand nand_2 (nand_2_out, B, B);
  nand nand_3 (nand_3_out, C, C);
  nand nand_4 (nand_4_out, B, B);
  nand nand_5 (nand_5_out, A, A);
  nand nand_6 (nand_6_out, C, C);
  nand nand_7 (nand_7_out, A, A);
  nand nand_8 (nand_8_out, B, B);
  nand nand_9 (nand_9_out, B, B);
  nand nand_10 (nand_10_out, C, C);
  nand nand_11 (nand_11_out, B, B);
  nand nand_12 (nand_12_out, A, A);
  nand nand_13 (nand_13_out, A, A);
  nand nand_14 (nand_14_out, B, B);
  nand nand_15 (nand_15_out, A, A);
  nand nand_16 (nand_16_out, B, B);
  nand nand_17 (nand_17_out, C, C);
  nand nand_18 (nand_18_out, A, B);
  nand nand_19 (nand_19_out, A, A);
  nand nand_20 (nand_20_out, C, C);
  nand nand_21 (nand_21_out, A, A);
  nand nand_22 (nand_22_out, B, B);
  nand nand_23 (nand_23_out, A, A);
  nand nand_24 (nand_24_out, A, A);
  nand nand_25 (nand_25_out, B, B);
  nand nand_26 (nand_26_out, A, A);
  nand nand_27 (nand_27_out, B, B);
  nand nand_28 (nand_28_out, nand_1_out, B);
  nand nand_29 (nand_29_out, nand_2_out, nand_3_out);
  nand nand_30 (nand_30_out, A, nand_4_out);
  nand nand_31 (nand_31_out, nand_5_out, nand_6_out);
  nand nand_32 (nand_32_out, nand_7_out, C);
  nand nand_33 (nand_33_out, A, nand_8_out);
  nand nand_34 (nand_34_out, nand_9_out, nand_10_out);
  nand nand_35 (nand_35_out, A, nand_11_out);
  nand nand_36 (nand_36_out, nand_12_out, C);
  nand nand_37 (nand_37_out, nand_13_out, nand_14_out);
  nand nand_38 (nand_38_out, nand_15_out, C);
  nand nand_39 (nand_39_out, nand_16_out, nand_17_out);
  nand nand_40 (nand_40_out, nand_18_out, nand_18_out);
  nand nand_41 (nand_41_out, C, C);
  nand nand_42 (nand_42_out, nand_19_out, nand_20_out);
  nand nand_43 (nand_43_out, nand_21_out, B);
  nand nand_44 (nand_44_out, A, nand_22_out);
  nand nand_45 (nand_45_out, nand_23_out, C);
  nand nand_46 (nand_46_out, nand_24_out, nand_25_out);
  nand nand_47 (nand_47_out, nand_26_out, B);
  nand nand_48 (nand_48_out, A, nand_27_out);
  nand nand_49 (nand_49_out, A, A);
  nand nand_50 (nand_50_out, nand_28_out, nand_28_out);
  nand nand_51 (nand_51_out, nand_29_out, nand_29_out);
  nand nand_52 (nand_52_out, D, D);
  nand nand_53 (nand_53_out, nand_30_out, nand_30_out);
  nand nand_54 (nand_54_out, C, C);
  nand nand_55 (nand_55_out, A, A);
  nand nand_56 (nand_56_out, B, B);
  nand nand_57 (nand_57_out, nand_31_out, nand_31_out);
  nand nand_58 (nand_58_out, D, D);
  nand nand_59 (nand_59_out, nand_32_out, nand_32_out);
  nand nand_60 (nand_60_out, nand_33_out, nand_33_out);
  nand nand_61 (nand_61_out, D, D);
  nand nand_62 (nand_62_out, A, A);
  nand nand_63 (nand_63_out, D, D);
  nand nand_64 (nand_64_out, nand_34_out, nand_34_out);
  nand nand_65 (nand_65_out, D, D);
  nand nand_66 (nand_66_out, nand_35_out, nand_35_out);
  nand nand_67 (nand_67_out, C, C);
  nand nand_68 (nand_68_out, nand_36_out, nand_36_out);
  nand nand_69 (nand_69_out, D, D);
  nand nand_70 (nand_70_out, nand_37_out, nand_37_out);
  nand nand_71 (nand_71_out, B, B);
  nand nand_72 (nand_72_out, C, C);
  nand nand_73 (nand_73_out, B, B);
  nand nand_74 (nand_74_out, A, A);
  nand nand_75 (nand_75_out, C, C);
  nand nand_76 (nand_76_out, nand_38_out, nand_38_out);
  nand nand_77 (nand_77_out, D, D);
  nand nand_78 (nand_78_out, nand_39_out, nand_39_out);
  nand nand_79 (nand_79_out, D, D);
  nand nand_80 (nand_80_out, nand_40_out, nand_41_out);
  nand nand_81 (nand_81_out, nand_42_out, nand_42_out);
  nand nand_82 (nand_82_out, D, D);
  nand nand_83 (nand_83_out, nand_43_out, nand_43_out);
  nand nand_84 (nand_84_out, D, D);
  nand nand_85 (nand_85_out, nand_44_out, nand_44_out);
  nand nand_86 (nand_86_out, C, C);
  nand nand_87 (nand_87_out, nand_45_out, nand_45_out);
  nand nand_88 (nand_88_out, D, D);
  nand nand_89 (nand_89_out, nand_46_out, nand_46_out);
  nand nand_90 (nand_90_out, nand_47_out, nand_47_out);
  nand nand_91 (nand_91_out, C, C);
  nand nand_92 (nand_92_out, nand_48_out, nand_48_out);
  nand nand_93 (nand_93_out, C, C);
  nand nand_94 (nand_94_out, nand_49_out, C);
  nand nand_95 (nand_95_out, nand_50_out, D);
  nand nand_96 (nand_96_out, nand_51_out, nand_52_out);
  nand nand_97 (nand_97_out, nand_53_out, nand_54_out);
  nand nand_98 (nand_98_out, nand_55_out, nand_56_out);
  nand nand_99 (nand_99_out, nand_57_out, nand_58_out);
  nand nand_100 (nand_100_out, nand_59_out, D);
  nand nand_101 (nand_101_out, nand_60_out, nand_61_out);
  nand nand_102 (nand_102_out, nand_62_out, B);
  nand nand_103 (nand_103_out, A, nand_63_out);
  nand nand_104 (nand_104_out, nand_64_out, nand_65_out);
  nand nand_105 (nand_105_out, nand_66_out, nand_67_out);
  nand nand_106 (nand_106_out, nand_68_out, nand_69_out);
  nand nand_107 (nand_107_out, nand_70_out, C);
  nand nand_108 (nand_108_out, nand_71_out, nand_72_out);
  nand nand_109 (nand_109_out, A, nand_73_out);
  nand nand_110 (nand_110_out, nand_74_out, B);
  nand nand_111 (nand_111_out, nand_75_out, D);
  nand nand_112 (nand_112_out, nand_76_out, nand_77_out);
  nand nand_113 (nand_113_out, nand_78_out, nand_79_out);
  nand nand_114 (nand_114_out, nand_80_out, nand_80_out);
  nand nand_115 (nand_115_out, nand_81_out, nand_82_out);
  nand nand_116 (nand_116_out, nand_83_out, nand_84_out);
  nand nand_117 (nand_117_out, nand_85_out, nand_86_out);
  nand nand_118 (nand_118_out, nand_87_out, nand_88_out);
  nand nand_119 (nand_119_out, nand_89_out, C);
  nand nand_120 (nand_120_out, nand_90_out, nand_91_out);
  nand nand_121 (nand_121_out, nand_92_out, nand_93_out);
  nand nand_122 (nand_122_out, nand_94_out, nand_95_out);
  nand nand_123 (nand_123_out, nand_96_out, nand_97_out);
  nand nand_124 (nand_124_out, nand_98_out, nand_99_out);
  nand nand_125 (nand_125_out, nand_100_out, nand_101_out);
  nand nand_126 (nand_126_out, nand_102_out, nand_103_out);
  nand nand_127 (nand_127_out, nand_104_out, nand_105_out);
  nand nand_128 (nand_128_out, nand_106_out, nand_107_out);
  nand nand_129 (nand_129_out, nand_108_out, nand_108_out);
  nand nand_130 (nand_130_out, D, D);
  nand nand_131 (nand_131_out, nand_109_out, nand_109_out);
  nand nand_132 (nand_132_out, C, C);
  nand nand_133 (nand_133_out, nand_110_out, nand_110_out);
  nand nand_134 (nand_134_out, nand_111_out, nand_111_out);
  nand nand_135 (e, nand_112_out, nand_113_out);
  nand nand_136 (nand_136_out, nand_114_out, nand_115_out);
  nand nand_137 (nand_137_out, nand_116_out, nand_117_out);
  nand nand_138 (nand_138_out, nand_118_out, nand_119_out);
  nand nand_139 (nand_139_out, nand_120_out, nand_121_out);
  nand nand_140 (nand_140_out, nand_122_out, nand_122_out);
  nand nand_141 (nand_141_out, nand_123_out, nand_123_out);
  nand nand_142 (nand_142_out, nand_124_out, nand_124_out);
  nand nand_143 (nand_143_out, nand_125_out, nand_125_out);
  nand nand_144 (nand_144_out, nand_126_out, nand_126_out);
  nand nand_145 (nand_145_out, nand_127_out, nand_127_out);
  nand nand_146 (nand_146_out, nand_128_out, nand_128_out);
  nand nand_147 (nand_147_out, nand_129_out, nand_130_out);
  nand nand_148 (nand_148_out, nand_131_out, nand_132_out);
  nand nand_149 (nand_149_out, nand_133_out, nand_134_out);
  nand nand_150 (nand_150_out, nand_136_out, nand_136_out);
  nand nand_151 (nand_151_out, nand_137_out, nand_137_out);
  nand nand_152 (nand_152_out, nand_138_out, nand_138_out);
  nand nand_153 (nand_153_out, nand_139_out, nand_139_out);
  nand nand_154 (a_2, nand_140_out, nand_141_out);
  nand nand_155 (b_2, nand_142_out, nand_143_out);
  nand nand_156 (c_2, nand_144_out, nand_145_out);
  nand nand_157 (nand_157_out, nand_146_out, nand_147_out);
  nand nand_158 (nand_158_out, nand_148_out, nand_149_out);
  nand nand_159 (f, nand_150_out, nand_151_out);
  nand nand_160 (g, nand_152_out, nand_153_out);
  nand nand_161 (nand_161_out, nand_157_out, nand_157_out);
  nand nand_162 (nand_162_out, nand_158_out, nand_158_out);
  nand nand_163 (d_2, nand_161_out, nand_162_out);
endmodule
