// Logisim project Example3-7VerifyBCDToExcess3.circ as structural Verilog: 1 circuit, main circuit main
module main (
  input  A,
  input  B,
  input  C,
  input  D,
  output W,
  output X,
  output Y,
  output Z
);

  wire nand_1_out, nand_2_out, nand_3_out, nand_4_out, nand_5_out, not_1_out, not_2_out, not_3_out, not_5_out;

  not not_1 (not_1_out, A);
  not not_2 (not_2_out, B);
  not not_3 (not_3_out, C);
  not not_4 (Z, D);
  not not_5 (not_5_out, nand_2_out);
  nand nand_1 (nand_1_out, B, nand_2_out);
  nand nand_2 (nand_2_out, not_3_out, Z);
  nand nand_3 (nand_3_out, not_2_out, nand_2_out);
  nand nand_4 (nand_4_out, B, not_5_out);
  nand nand_5 (nand_5_out, C, D);
  nand nand_6 (W, not_1_out, nand_1_out);
  nand nand_7 (Y, not_5_out, nand_5_out);
  nand nand_8 (X, nand_3_out, nand_4_out);
endmodule
