// Logisim project Example3-8HomeEnabler.circ as structural Verilog: 1 circuit, main circuit main
module main (
  input  Enabler,
  input  in_2,
  input  in_3,
  output H
);

  wire and_1_out, and_2_out, and_3_out, and_4_out, and_5_out, and_6_out, and_7_out, and_8_out, not_1_out,
       not_2_out;

  not not_1 (not_1_out, in_2);
  not not_2 (not_2_out, in_3);
  and and_1 (and_1_out, not_1_out, not_2_out);
  and and_2 (and_2_out, not_1_out, in_3);
  and and_3 (and_3_out, in_2, not_2_out);
  and and_4 (and_4_out, in_2, in_3);
  and and_5 (and_5_out, and_1_out, Enabler);
  and and_6 (and_6_out, and_2_out, Enabler);
  and and_7 (and_7_out, and_3_out, Enabler);
  and and_8 (and_8_out, and_4_out, Enabler);
  or or_1 (H, and_5_out, and_6_out, and_7_out, and_8_out);
endmodule
