// Logisim project Example2-4.circ as structural Verilog: 1 circuit, main circuit main
module main (
  input  A,
  input  B,
  output F
);

  wire and_1_out, and_2_out;

  and and_1 (and_1_out, ~A, B);  // AND_Gate
  and and_2 (and_2_out, A, ~B);  // AND_Gate
  or or_1 (F, and_1_out, and_2_out);
endmodule
