// Logisim project Example2-7ThreeVariableSimplification.circ as structural Verilog: 1 circuit, main circuit main
module main (
  input  A,
  input  C,
  input  B,
  output out_4
);

  wire and_1_out, and_2_out, and_3_out, not_1_out, not_2_out, not_3_out;

  not not_1 (not_1_out, A);
  and and_1 (and_1_out, not_1_out, C);
  and and_2 (and_2_out, A, not_2_out);
  not not_2 (not_2_out, B);
  and and_3 (and_3_out, B, not_3_out);
  not not_3 (not_3_out, C);
  or or_1 (out_4, and_1_out, and_2_out, and_3_out);
endmodule
