// Logisim project SixtyFourBit.circ as structural Verilog: 1 circuit, main circuit main
module main (
  input  in_1,
  input  [5:0] Input,
  output [31:0] out_3,
  output [31:0] out_4
);

  wire decoder_1_out0, decoder_1_out1;

  Decoder #(.disabled(0)) decoder_1 (.out0(decoder_1_out0), .out1(decoder_1_out1), .sel(Input[5]), .en(in_1));
  Decoder #(.select(5), .disabled(0)) decoder_2 (
    .out0(out_3[31]), .out1(out_3[30]), .out2(out_3[29]), .out3(out_3[28]), .out4(out_3[27]),
    .out5(out_3[26]), .out6(out_3[25]), .out7(out_3[24]), .out8(out_3[23]), .out9(out_3[22]),
    .out10(out_3[21]), .out11(out_3[20]), .out12(out_3[19]), .out13(out_3[18]), .out14(out_3[17]),
    .out15(out_3[16]), .out16(out_3[15]), .out17(out_3[14]), .out18(out_3[13]), .out19(out_3[12]),
    .out20(out_3[11]), .out21(out_3[10]), .out22(out_3[9]), .out23(out_3[8]), .out24(out_3[7]),
    .out25(out_3[6]), .out26(out_3[5]), .out27(out_3[4]), .out28(out_3[3]), .out29(out_3[2]),
    .out30(out_3[1]), .out31(out_3[0]), .sel(Input[4:0]), .en(decoder_1_out1));
  Decoder #(.select(5), .disabled(0)) decoder_3 (
    .out0(out_4[31]), .out1(out_4[30]), .out2(out_4[29]), .out3(out_4[28]), .out4(out_4[27]),
    .out5(out_4[26]), .out6(out_4[25]), .out7(out_4[24]), .out8(out_4[23]), .out9(out_4[22]),
    .out10(out_4[21]), .out11(out_4[20]), .out12(out_4[19]), .out13(out_4[18]), .out14(out_4[17]),
    .out15(out_4[16]), .out16(out_4[15]), .out17(out_4[14]), .out18(out_4[13]), .out19(out_4[12]),
    .out20(out_4[11]), .out21(out_4[10]), .out22(out_4[9]), .out23(out_4[8]), .out24(out_4[7]),
    .out25(out_4[6]), .out26(out_4[5]), .out27(out_4[4]), .out28(out_4[3]), .out29(out_4[2]),
    .out30(out_4[1]), .out31(out_4[0]), .sel(Input[4:0]), .en(decoder_1_out0));
endmodule
