// Logisim project SetResetLatchNOR.circ as structural Verilog: 1 circuit, main circuit main
module main (
  input  S,
  input  R,
  output Q,
  output QBar
);

  nor nor_1 (Q, S, QBar);
  nor nor_2 (QBar, Q, R);
endmodule
