// Logisim project Example2-9FourVariableMapSimplification2.circ as structural Verilog: 1 circuit, main circuit main
module main (
  input  A,
  input  C,
  input  B,
  input  D,
  output out_5
);

  wire and_1_out, and_2_out, and_3_out, not_1_out, not_2_out, not_3_out, not_4_out;

  not not_1 (not_1_out, A);
  not not_2 (not_2_out, C);
  not not_3 (not_3_out, B);
  and and_1 (and_1_out, not_3_out, not_4_out);
  not not_4 (not_4_out, D);
  and and_2 (and_2_out, not_1_out, not_2_out);
  and and_3 (and_3_out, C, D);
  or or_1 (out_5, and_2_out, and_3_out, and_1_out);
endmodule
