// Logisim project 4BitEqualityComparatorNAND.circ as structural Verilog
module FourBitCompareNand (
  input  A,
  input  B,
  input  C,
  input  D,
  input  E,
  output F
);

  wire nand_1_out, nand_2_out, nand_3_out, nand_4_out, nand_5_out, nand_6_out, nand_7_out;

  nand nand_1 (nand_1_out, A, B);
  nand nand_2 (nand_2_out, A, B);
  nand nand_3 (nand_3_out, D, D);
  nand nand_4 (nand_4_out, A, B);
  nand nand_5 (nand_5_out, nand_1_out, C);
  nand nand_6 (nand_6_out, nand_2_out, nand_3_out);
  nand nand_7 (nand_7_out, E, E);
  nand nand_8 (F, nand_4_out, nand_5_out, nand_6_out, nand_7_out);
endmodule
