// Logisim project BCDtoExcess3.circ as structural Verilog
module W (
  input  A,
  input  B,
  input  C,
  input  D,
  output W,
  output X,
  output Y,
  output Z
);

  wire and_1_out, and_2_out, and_3_out, and_4_out, and_5_out, and_6_out, and_7_out, not_1_out, not_2_out,
       not_3_out, not_4_out, not_5_out, not_6_out;

  and and_1 (and_1_out, B, D);
  and and_2 (and_2_out, B, C);
  not not_1 (not_1_out, B);
  and and_3 (and_3_out, not_1_out, D);
  not not_2 (not_2_out, B);
  and and_4 (and_4_out, not_2_out, C);
  not not_3 (not_3_out, C);
  and and_5 (and_5_out, B, not_3_out, not_4_out);
  not not_4 (not_4_out, D);
  not not_5 (not_5_out, C);
  and and_6 (and_6_out, not_5_out, not_6_out);
  not not_6 (not_6_out, D);
  and and_7 (and_7_out, C, D);
  not not_7 (Z, D);
  or or_1 (W, and_1_out, and_2_out, A);
  or or_2 (X, and_3_out, and_4_out, and_5_out);
  or or_3 (Y, and_6_out, and_7_out);
endmodule

module X (
  input  A,
  input  B,
  input  C,
  input  D,
  output W,
  output X,
  output Y,
  output Z
);

  wire and_1_out, and_2_out, and_3_out, and_4_out, and_5_out, and_6_out, and_7_out, not_1_out, not_2_out,
       not_3_out, not_4_out, not_5_out, not_6_out;

  and and_1 (and_1_out, B, D);
  and and_2 (and_2_out, B, C);
  not not_1 (not_1_out, B);
  and and_3 (and_3_out, not_1_out, D);
  not not_2 (not_2_out, B);
  and and_4 (and_4_out, not_2_out, C);
  and and_5 (and_5_out, B, not_3_out, not_4_out);
  not not_3 (not_3_out, C);
  not not_4 (not_4_out, D);
  not not_5 (not_5_out, C);
  and and_6 (and_6_out, not_5_out, not_6_out);
  not not_6 (not_6_out, D);
  and and_7 (and_7_out, C, D);
  not not_7 (Z, D);
  or or_1 (W, and_1_out, and_2_out, A);
  or or_2 (X, and_3_out, and_4_out, and_5_out);
  or or_3 (Y, and_6_out, and_7_out);
endmodule

module Y (
  input  A,
  input  B,
  input  C,
  input  D,
  output W,
  output X,
  output Y,
  output Z
);

  wire and_1_out, and_2_out, and_3_out, and_4_out, and_5_out, and_6_out, and_7_out, not_1_out, not_2_out,
       not_3_out, not_4_out, not_5_out, not_6_out;

  and and_1 (and_1_out, B, D);
  and and_2 (and_2_out, B, C);
  not not_1 (not_1_out, B);
  and and_3 (and_3_out, not_1_out, D);
  not not_2 (not_2_out, B);
  and and_4 (and_4_out, not_2_out, C);
  not not_3 (not_3_out, C);
  and and_5 (and_5_out, B, not_3_out, not_4_out);
  not not_4 (not_4_out, D);
  not not_5 (not_5_out, C);
  and and_6 (and_6_out, not_5_out, not_6_out);
  not not_6 (not_6_out, D);
  and and_7 (and_7_out, C, D);
  not not_7 (Z, D);
  or or_1 (W, and_1_out, and_2_out, A);
  or or_2 (X, and_3_out, and_4_out, and_5_out);
  or or_3 (Y, and_6_out, and_7_out);
endmodule

module Z (
  input  A,
  input  B,
  input  C,
  input  D,
  output W,
  output X,
  output Y,
  output Z
);

  wire and_1_out, and_2_out, and_3_out, and_4_out, and_5_out, and_6_out, and_7_out, not_1_out, not_2_out,
       not_3_out, not_4_out, not_5_out, not_6_out;

  and and_1 (and_1_out, B, D);
  and and_2 (and_2_out, B, C);
  not not_1 (not_1_out, B);
  and and_3 (and_3_out, not_1_out, D);
  not not_2 (not_2_out, B);
  and and_4 (and_4_out, not_2_out, C);
  and and_5 (and_5_out, B, not_3_out, not_4_out);
  not not_3 (not_3_out, C);
  not not_4 (not_4_out, D);
  not not_5 (not_5_out, C);
  and and_6 (and_6_out, not_5_out, not_6_out);
  not not_6 (not_6_out, D);
  and and_7 (and_7_out, C, D);
  not not_7 (Z, D);
  or or_1 (W, and_1_out, and_2_out, A);
  or or_2 (X, and_3_out, and_4_out, and_5_out);
  or or_3 (Y, and_6_out, and_7_out);
endmodule

module BCD3 (
  input  A,
  input  B,
  input  C,
  input  D,
  output W,
  output X,
  output Y,
  output Z
);

  wire and_1_out, and_2_out, and_3_out, and_4_out, and_5_out, and_6_out, and_7_out, and_8_out, not_1_out,
       not_2_out, not_3_out, not_4_out, not_5_out, not_6_out, or_1_out, or_3_out;

  and and_1 (and_1_out, B, D);
  and and_2 (and_2_out, B, C);
  not not_1 (not_1_out, B);
  and and_3 (and_3_out, not_1_out, D);
  not not_2 (not_2_out, B);
  and and_4 (and_4_out, not_2_out, C);
  and and_5 (and_5_out, B, not_3_out);
  not not_3 (not_3_out, C);
  not not_4 (not_4_out, D);
  not not_5 (not_5_out, C);
  and and_6 (and_6_out, not_5_out, not_6_out);
  not not_6 (not_6_out, D);
  and and_7 (and_7_out, C, D);
  not not_7 (Z, D);
  or or_1 (or_1_out, and_1_out, and_2_out);
  or or_2 (W, or_1_out, A);
  or or_3 (or_3_out, and_3_out, and_4_out);
  and and_8 (and_8_out, and_5_out, not_4_out);
  or or_4 (Y, and_6_out, and_7_out);
  or or_5 (X, or_3_out, and_8_out);
endmodule
