// Logisim project BooleanAsPowerWindow.circ as structural Verilog: 1 circuit, main circuit main
module main (
  output L
);

  wire clock_1_out, D_out, nand_1_out;

  Button D (.out(D_out));
  Clock clock_1 (.out(clock_1_out));
  nand nand_1 (nand_1_out, clock_1_out, D_out);
  nand nand_2 (L, nand_1_out, nand_1_out);
endmodule
