// Logisim project BooleanAsPowerWindowLegacy.circ as structural Verilog: 1 circuit, main circuit main
module main (
);

  wire and_1_out, clock_1_out, D_out, xor_1_out, xor_2_out;

  Button D (.out(D_out));
  Clock clock_1 (.out(clock_1_out));
  and and_1 (and_1_out, clock_1_out, D_out);
  xor xor_1 (xor_1_out, and_1_out, xor_2_out);
  xor xor_2 (xor_2_out, and_1_out, xor_1_out);
endmodule
