// Logisim project MasterSlaveSetReset.circ as structural Verilog: 1 circuit, main circuit main
module main (
  input  S,
  input  R,
  input  C,
  output out_4,
  output out_5
);

  wire not_1_out, s_r_ff_1_q, s_r_ff_1_qn;

  S_R_Flip_Flop s_r_ff_1 (.S(S), .R(R), .clk(C), .Q(s_r_ff_1_q), .Qn(s_r_ff_1_qn));  // open: reset, preset
  not not_1 (not_1_out, C);
  S_R_Flip_Flop s_r_ff_2 (
    .S(s_r_ff_1_q), .R(not_1_out), .clk(s_r_ff_1_qn), .Q(out_4), .Qn(out_5));  // open: reset, preset
endmodule
