// Logisim project RamModuleWithRSFlipFlop.circ as structural Verilog: 2 circuits, main circuit main
// BC
module main (
  input  twoTwo,
  input  twoOne,
  input  twoZero,
  input  Read,
  input  Clock,
  input  [1:0] DecoderInput,
  output out_7,
  output out_8,
  output out_9
);

  wire basiccell_1_out_5, basiccell_2_out_5, basiccell_3_out_5, basiccell_4_out_5, basiccell_5_out_5,
       basiccell_6_out_5, basiccell_7_out_5, basiccell_8_out_5, basiccell_9_out_5, basiccell_10_out_5,
       basiccell_11_out_5, basiccell_12_out_5, decoder_1_out0, decoder_1_out1, decoder_1_out2, decoder_1_out3;

  BasicCell basiccell_1 (
    .Input(twoTwo), .Select(decoder_1_out0), .Read(Read), .out_5(basiccell_1_out_5));  // open: Clock
  BasicCell basiccell_2 (
    .Input(twoTwo), .Select(decoder_1_out1), .Read(Read), .out_5(basiccell_2_out_5));  // open: Clock
  BasicCell basiccell_3 (
    .Input(twoTwo), .Select(decoder_1_out2), .Read(Read), .Clock(Clock), .out_5(basiccell_3_out_5));
  BasicCell basiccell_4 (
    .Input(twoTwo), .Select(decoder_1_out3), .Read(Read), .Clock(Clock), .out_5(basiccell_4_out_5));
  or or_1 (out_7, basiccell_4_out_5, basiccell_3_out_5, basiccell_2_out_5, basiccell_1_out_5);
  BasicCell basiccell_5 (
    .Input(twoOne), .Select(decoder_1_out0), .Read(Read), .out_5(basiccell_5_out_5));  // open: Clock
  BasicCell basiccell_6 (
    .Input(twoOne), .Select(decoder_1_out1), .Read(Read), .out_5(basiccell_6_out_5));  // open: Clock
  BasicCell basiccell_7 (
    .Input(twoOne), .Select(decoder_1_out2), .Read(Read), .Clock(Clock), .out_5(basiccell_7_out_5));
  BasicCell basiccell_8 (
    .Input(twoOne), .Select(decoder_1_out3), .Read(Read), .Clock(Clock), .out_5(basiccell_8_out_5));
  or or_2 (out_8, basiccell_8_out_5, basiccell_7_out_5, basiccell_6_out_5, basiccell_5_out_5);
  BasicCell basiccell_9 (
    .Input(twoZero), .Select(decoder_1_out0), .Read(Read), .Clock(Clock), .out_5(basiccell_9_out_5));
  BasicCell basiccell_10 (
    .Input(twoZero), .Select(decoder_1_out1), .Read(Read), .Clock(Clock), .out_5(basiccell_10_out_5));
  BasicCell basiccell_11 (
    .Input(twoZero), .Select(decoder_1_out2), .Read(Read), .Clock(Clock), .out_5(basiccell_11_out_5));
  BasicCell basiccell_12 (
    .Input(twoZero), .Select(decoder_1_out3), .Read(Read), .Clock(Clock), .out_5(basiccell_12_out_5));
  or or_3 (out_9, basiccell_12_out_5, basiccell_11_out_5, basiccell_10_out_5, basiccell_9_out_5);
  Decoder #(.select(2)) decoder_1 (
    .out0(decoder_1_out0), .out1(decoder_1_out1), .out2(decoder_1_out2), .out3(decoder_1_out3),
    .sel(DecoderInput));  // open: en
endmodule

// BC
module BasicCell (
  input  Select,
  input  Input,
  input  Read,
  input  Clock,
  output out_5
);

  wire and_1_out, and_2_out, not_1_out, s_r_ff_1_q;

  and and_1 (and_1_out, Select, Input, not_1_out);
  and and_2 (and_2_out, Select, ~Input, not_1_out);  // AND_Gate
  not not_1 (not_1_out, Read);
  S_R_Flip_Flop s_r_ff_1 (.S(and_1_out), .R(and_2_out), .clk(Clock), .Q(s_r_ff_1_q));  // open: reset, Qn, preset
  and and_3 (out_5, Select, s_r_ff_1_q, Read);
endmodule
