// Logisim project Multiplexer.circ as structural Verilog: 3 circuits, main circuit main
module main (
  input  s0,
  input  s1,
  input  data1,
  input  data2,
  input  data3,
  input  data4,
  output Y
);

  wire twobyfourdecoder_1_output00, twobyfourdecoder_1_output01, twobyfourdecoder_1_output10,
       twobyfourdecoder_1_output11;

  TwoByFourDecoder twobyfourdecoder_1 (
    .s0(s0), .s1(s1), .output00(twobyfourdecoder_1_output00), .output01(twobyfourdecoder_1_output01),
    .output10(twobyfourdecoder_1_output10), .output11(twobyfourdecoder_1_output11));
  FourByTwoAndOr fourbytwoandor_1 (
    .control0(twobyfourdecoder_1_output00), .i0(data1), .control1(twobyfourdecoder_1_output01), .i1(data2),
    .control2(twobyfourdecoder_1_output10), .i2(data3), .control3(twobyfourdecoder_1_output11), .i3(data4),
    .Y(Y));
endmodule

// AndOr
module FourByTwoAndOr (
  input  control0,
  input  i0,
  input  control1,
  input  i1,
  input  control2,
  input  i2,
  input  control3,
  input  i3,
  output Y
);

  wire and_1_out, and_2_out, and_3_out, and_4_out, or_1_out, or_2_out;

  and and_1 (and_1_out, control0, i0);
  and and_2 (and_2_out, control1, i1);
  and and_3 (and_3_out, control2, i2);
  and and_4 (and_4_out, control3, i3);
  or or_1 (or_1_out, and_1_out, and_2_out);
  or or_2 (or_2_out, and_3_out, and_4_out);
  or or_3 (Y, or_1_out, or_2_out);
endmodule

// Decoder
module TwoByFourDecoder (
  input  s0,
  input  s1,
  output output00,
  output output01,
  output output10,
  output output11
);

  wire not_1_out, not_2_out;

  not not_1 (not_1_out, s0);
  not not_2 (not_2_out, s1);
  and and_1 (output00, not_1_out, not_2_out);
  and and_2 (output01, not_1_out, s1);
  and and_3 (output10, s0, not_2_out);
  and and_4 (output11, s1, s0);
endmodule
